# Fritzing sketch plan_electrique (saved by Fritzing 0.9.3b)
breadboards: 1

parts:
  J2 = Infrared Proximity Sensor
  J3 = Infrared Proximity Sensor
  Composant2 = LED Matrix - Serial Interface - Red/Green/Blue
  Composant3 = LED Matrix - Serial Interface - Red/Green/Blue  # not connected
  Composant4 = LED Matrix - Serial Interface - Red/Green/Blue  # not connected
  Composant5 = LED Matrix - Serial Interface - Red/Green/Blue
  U1 = WS2812_RGB_LED_matrix_1x8
  U3 = WS2812_RGB_LED_matrix_1x8
  U4 = WS2812_RGB_LED_matrix_1x8
  Composant6 = Arduino Mega 2560 (Rev3)
  U6 = LM2596 step down module
  U2 = WS2812_RGB_LED_matrix_1x8
  J6 = Infrared Proximity Sensor
  R2 = Resistor [tolerance=±5% resistance=220 package=THT]
  R3 = Resistor [tolerance=±5% resistance=220 package=THT]
  R4 = Resistor [tolerance=±5% resistance=220 package=THT]
  R8 = Resistor [tolerance=±5% resistance=220 package=THT]
  U7 = WS2812_RGB_LED_matrix_1x8
  U8 = WS2812_RGB_LED_matrix_1x8
  U9 = WS2812_RGB_LED_matrix_1x8
  U10 = WS2812_RGB_LED_matrix_1x8
  J7 = Infrared Proximity Sensor
  R9 = Resistor [tolerance=±5% resistance=220 package=THT]
  R10 = Resistor [tolerance=±5% resistance=220 package=THT]
  R11 = Resistor [tolerance=±5% resistance=220 package=THT]
  R12 = Resistor [tolerance=±5% resistance=220 package=THT]
  R13 = Resistor [tolerance=±5% resistance=220 package=THT]

nets:
  N1: J2.Vout, Composant6.A2
  N2: J3.Vout, Composant6.A1
  VCC: Composant2.VCC, Composant5.VCC, Composant6.VIN, U2.connector1, J7.Vcc
  N3: Composant2.SCK, Composant6.D52
  N4: Composant2.CS, R13.Pin_1
  N5: Composant2.MISO, Composant6.D53
  GND: Composant2.GND, Composant6.GND, U6.connector3, J6.GND
  N6: U1.connector0, U2.connector3
  N7: U1.connector2, R3.Pin_1
  N8: U3.connector2, R4.Pin_1
  N9: U4.connector2, R2.Pin_1
  N10: Composant6.A0, J6.Vout
  N11: Composant6.A3, J7.Vout
  N12: Composant6.D9_PWM, R9.Pin_1
  N13: Composant6.D8_PWM, R11.Pin_1
  N14: Composant6.D2_PWM, R3.Pin_0
  N15: Composant6.D3_PWM, R2.Pin_0
  N16: Composant6.D4_PWM, R4.Pin_0
  N17: Composant6.D5_PWM, R8.Pin_0
  N18: Composant6.D6_PWM, R12.Pin_1
  N19: Composant6.D7_PWM, R10.Pin_1
  N20: Composant6.D51, R13.Pin_0
  N21: U2.connector2, R8.Pin_1
  N22: U7.connector1, U10.connector1
  N23: U7.connector2, R12.Pin_0
  N24: U7.connector3, U10.connector0
  N25: U8.connector2, R10.Pin_0
  N26: U9.connector2, R11.Pin_0
  N27: U10.connector2, R9.Pin_0
